# Fritzing sketch puzzlebox (saved by Fritzing 0.9.2b)
circuit board: 6cm x 2.59999cm
breadboards: 1

parts:
  Resonator = Resonator [frequency="16 Mhz" package=THT]
  USB = USB connector [package=THT]
  atmega328p-pu = atmega328 [package=dip]
  Trellis_pin_header = female pin header, 4 pins [form="♀ (female)"]

nets:
  N1: Resonator.0, atmega328p-pu.XLAT1
  GND: Resonator.GND, USB.GND, USB.chassis5, USB.chassis6, atmega328p-pu.GND, Trellis_pin_header.pin3
  N2: Resonator.pin_1, atmega328p-pu.XLAT2
  5V: USB.5V, atmega328p-pu.VCC, atmega328p-pu.AVCC, Trellis_pin_header.pin4
  N3: atmega328p-pu.A4, Trellis_pin_header.pin1
  N4: atmega328p-pu.A5, Trellis_pin_header.pin2

notes:
  pussel 1.0
